# Fritzing sketch circuit_schematics_melissa,allyson,sahara (saved by Fritzing 0.9.3b)
breadboards: 1

parts:
  LED1 = LED - 5mm [color="Red (633nm)" package="5 mm [THT]"]
  LED2 = LED - 5mm [color="Red (633nm)" package="5 mm [THT]"]
  R1 = Resistor [tolerance=±5% resistance=220 package=THT]
  R2 = Resistor [tolerance=±5% resistance=220 package=THT]
  IC1 = L293D [package=THT]
  M1 = DC Motor
  M2 = DC Motor
  Part1 = Arduino Uno (Rev3) - ICSP
  BAT1 = BC9VPC [package=bc9vpc]

nets:
  N1: LED1.cathode, R1.Pin_0
  N2: LED1.anode, Part1.D13/SCK
  N3: LED2.cathode, R2.Pin_1
  N4: LED2.anode, Part1.D12/MISO
  N5: R1.Pin_1, R2.Pin_0, IC1.0V, Part1.GND, BAT1.V-
  N6: IC1.Enable_1, Part1.D8
  N7: IC1.In_1, Part1.D2
  N8: IC1.Out_1_(_Controlled_by_Enable_1_), M2.pin_2
  N9: IC1.Out_2_(_Controlled_by_Enable_1_), M2.pin_1
  N10: IC1.In_2, Part1.D3_PWM
  N11: IC1.+Vmotor, BAT1.V+
  N12: IC1.Enable_2, Part1.D9_PWM
  N13: IC1.In_3, Part1.D4
  N14: IC1.Out_3_(_Controlled_by_Enable_2_), M1.pin_2
  N15: IC1.Out_4_(_Controlled_by_Enable_2_), M1.pin_1
  N16: IC1.In_4, Part1.D5_PWM
  N17: IC1.+V, Part1.5V
